# Fritzing sketch SimpleLFO (saved by Fritzing 0.9.4)
breadboards: 1

parts:
  IC1 = Dual Op-Amp [package=dip08]
  R1 = Resistor [tolerance=±5% resistance=6.8k package=THT]
  R2 = Resistor [tolerance=±5% resistance=1k package=THT]
  C1 = Film/Foil Capacitor [capacitance=100nF voltage=35V package="5mm [THT, pp]"]
  R3 = Resistor [tolerance=±5% resistance=15k package=THT]
  R4 = Resistor [tolerance=±5% resistance=33k package=THT]
  C3 = Ceramic Capacitor [capacitance=100nF package="100 mil [THT, multilayer]"]
  C4 = Ceramic Capacitor [capacitance=100nF package="100 mil [THT, multilayer]"]
  R5 = Resistor [tolerance=±5% resistance=47 package=THT]
  R6 = Rotary Potentiometer (Small) [maximum_resistance=100kΩ package=THT]
  R7 = Resistor [tolerance=±5% resistance=5.6k package=THT]
  R8 = Resistor [tolerance=±5% resistance=4.7k package=THT]
  C5 = Electrolytic Capacitor [capacitance=1µF package="100 mil [THT, electrolytic]"]
  C6 = Electrolytic Capacitor [capacitance=1µF package="100 mil [THT, electrolytic]"]

nets:
  N1: IC1.A_OUT, R2.Pin_1, C1.+, R3.Pin_1
  N2: IC1.A_-IN, R1.Pin_0, C1.-
  N3: IC1.A_+IN, IC1.B_-IN, C3.0, C4.1, R5.Pin_1, R8.Pin_0, C5.-, C6.+
  N4: IC1.A_V-, C3.1, C6.-
  N5: IC1.B_+IN, R3.Pin_0, R4.Pin_1
  N6: IC1.B_OUT, R4.Pin_0, R6.leg2, R7.Pin_1
  N7: IC1.A_V+, C4.0, C5.+
  N8: R1.Pin_1, R6.wiper
  N9: R5.Pin_0, R6.leg1
  N10: R7.Pin_0, R8.Pin_1

notes:
  SQR
  TRI
  GND
  +12V
  -12V
  GND
  50k/A
